# Fritzing sketch ExternalLED_WiFiKit32V2 (saved by Fritzing 0.9.4)
breadboards: 1

parts:
  R2 = Resistor [tolerance=±1% power=0.25 resistance=220 package=THT]
  LED2 = LED - 5mm [color="Red (633nm)" current=0.030 package="5 mm [THT]"]
  Heltec_WiFi_Kit_32_V1 = Heltec WiFi Kit 32 V2 [part_number=ZC-47]

nets:
  N1: R2.Pin_0, Heltec_WiFi_Kit_32_V1.pin_7
  N2: R2.Pin_1, LED2.anode
  N3: LED2.cathode, Heltec_WiFi_Kit_32_V1.pin_1
  N4: Heltec_WiFi_Kit_32_V1.pin_16, Heltec_WiFi_Kit_32_V1.pin_17
  N5: Heltec_WiFi_Kit_32_V1.pin_18, Heltec_WiFi_Kit_32_V1.pin_19
  N6: Heltec_WiFi_Kit_32_V1.pin_21, Heltec_WiFi_Kit_32_V1.pin_22
