# Fritzing sketch ExternalLED_Esp8266CroduinoNova (saved by Fritzing 0.9.4)
breadboards: 1

parts:
  LED4 = LED - 5mm [color="Red (633nm)" current=0.030 package="5 mm [THT]"]
  R1 = Resistor [tolerance=±1% power=0.25 resistance=330 package=THT]
  Esp8266_Croduino_Nova1 = Esp8266 Croduino NOVA

nets:
  N1: LED4.cathode, Esp8266_Croduino_Nova1.pin_19
  N2: LED4.anode, R1.Pin_1
  N3: R1.Pin_0, Esp8266_Croduino_Nova1.pin_16

custom parts:
  Esp8266 Croduino NOVA: Croduino with one button (RESET)
