# Fritzing sketch ExternalLED_Esp32NodeMCU (saved by Fritzing 0.9.4)
circuit board: 8.46667cm x 5.64444cm
breadboards: 2

parts:
  U1 = ESP32 NodeMCU Wide [part_number=ESP32-NodeMCU]
  R1 = Resistor [tolerance=±5% resistance=220 package="0805 [SMD]"]
  LED1 = smd LED [color="Red (633nm)" package="1206 [SMD]"]

nets:
  N1: U1.pin_14, U1.pin_32, U1.pin_38
  N2: U1.pin_31, R1.Pin_0
  N3: U1.pin_33, LED1.cathode
  N4: R1.Pin_1, LED1.anode

custom parts:
  ESP32 NodeMCU Wide: Esp32 NodeMCU, Generic 38-Pin ESP32 with wide format (only access to one side of pins on a breadboard) based on Stephen Lilley's HiLetgo ESP-WROOM-32 ESP32 ESP-32S Development Board.
