# Fritzing sketch AutomaticDimmer_HelTecWiFiKit32V2 (saved by Fritzing 0.9.9b)
breadboards: 1

parts:
  R1 = Photocell (LDR) [package=THT]
  R2 = Resistor [tolerance=±5% power=0.25 resistance=10k package=THT]
  R3 = Resistor [tolerance=±5% power=0.25 resistance=220 package=THT]
  LED1 = smd LED [color="Blue (430nm)" package="0603 [SMD]"]
  Heltec_WiFi_Kit_32_V1 = Heltec WiFi Kit 32 V2 [part_number=ZC-47]

nets:
  N1: R1.pin_0, LED1.cathode, Heltec_WiFi_Kit_32_V1.pin_36
  N2: R1.pin_1, R2.Pin_0, Heltec_WiFi_Kit_32_V1.pin_12
  N3: R2.Pin_1, Heltec_WiFi_Kit_32_V1.pin_34
  N4: R3.Pin_0, Heltec_WiFi_Kit_32_V1.pin_7
  N5: R3.Pin_1, LED1.anode
  N6: Heltec_WiFi_Kit_32_V1.pin_16, Heltec_WiFi_Kit_32_V1.pin_17
  N7: Heltec_WiFi_Kit_32_V1.pin_18, Heltec_WiFi_Kit_32_V1.pin_19
  N8: Heltec_WiFi_Kit_32_V1.pin_21, Heltec_WiFi_Kit_32_V1.pin_22
