# Fritzing sketch AutomaticDimmer_HelTecWiFiLoRa32V2 (saved by Fritzing 0.9.9b)
breadboards: 1

parts:
  R1 = Photocell (LDR) [package=THT]
  R2 = Resistor [tolerance=±5% power=0.25 resistance=10k package=THT]
  R3 = Resistor [tolerance=±5% power=0.25 resistance=220 package=THT]
  LED1 = smd LED [color="Blue (430nm)" package="0603 [SMD]"]
  Heltec_WiFi_LoRa_32_V1 = Heltec WiFi LoRa 32 V2 [part_number=HTIT-WB32LA]

nets:
  N1: R1.pin_0, LED1.cathode, Heltec_WiFi_LoRa_32_V1.pin_36
  N2: R1.pin_1, R2.Pin_0, Heltec_WiFi_LoRa_32_V1.pin_27
  N3: R2.Pin_1, Heltec_WiFi_LoRa_32_V1.pin_34
  N4: R3.Pin_0, Heltec_WiFi_LoRa_32_V1.pin_21, Heltec_WiFi_LoRa_32_V1.pin_22
  N5: R3.Pin_1, LED1.anode
  N6: Heltec_WiFi_LoRa_32_V1.pin_16, Heltec_WiFi_LoRa_32_V1.pin_17
  N7: Heltec_WiFi_LoRa_32_V1.pin_18, Heltec_WiFi_LoRa_32_V1.pin_19

custom parts:
  Heltec WiFi LoRa 32 V2: Heltec WiFi LoRa 32 V2 WiFi LoRa 32 is a classic IoT dev-board designed & produced by Heltec Automation(TM). It’s a highly integrated product based on ESP32 + SX127x, it has Wi-Fi, BLE, LoRa functions, also Li-Po battery management system, 0.96″ OLED are also included. It’s the best choice for smart cities, smart farms, smart home, and IoT makers.
